# Fritzing sketch tnt_game_electronics (saved by Fritzing 0.9.4)

parts:
  Part1 = Arduino Uno (Rev3)
  S1 = Toggle Switch [package=THT]
  VCC2 = 4 x AAA Battery Mount
  Keypad4x1 = Keypad Membran 4x4
  Grove1 = Grove OLED 128x96

nets:
  N1: Part1.D8, Keypad4x1.Pin2
  N2: Part1.D9_PWM, Keypad4x1.Pin1
  GND: Part1.GND, VCC2.-, Grove1.GND
  N3: Part1.D2, Keypad4x1.Pin8
  N4: Part1.D3_PWM, Keypad4x1.Pin7
  N5: Part1.D4, Keypad4x1.Pin6
  N6: Part1.D5_PWM, Keypad4x1.Pin5
  N7: Part1.D6_PWM, Keypad4x1.Pin4
  N8: Part1.D7, Keypad4x1.Pin3
  5V: Part1.5V, Grove1.VCC
  N9: Part1.VIN, S1.L2
  N10: S1.L1, VCC2.+

custom parts:
  Keypad Membran 4x4: Membrane Keypad 4x4 Matrix
